# Fritzing sketch button_driver (saved by Fritzing 0.9.3b)
circuit board: 7.83364cm x 5.80987cm
breadboards: 1

parts:
  KEY1 = male pin header, 3 pins [form="♂ (male)"]
  Q1 = NPN-Transistor [package="TO92 [THT]"]
  R2 = Resistor [tolerance=±5% resistance=220 package=THT]
  KEY3 = male pin header, 3 pins [form="♂ (male)"]
  Q2 = NPN-Transistor [package="TO92 [THT]"]
  R4 = Resistor [tolerance=±5% resistance=220 package=THT]
  KEY4 = male pin header, 3 pins [form="♂ (male)"]
  Q3 = NPN-Transistor [package="TO92 [THT]"]
  R6 = Resistor [tolerance=±5% resistance=220 package=THT]
  KEY5 = male pin header, 3 pins [form="♂ (male)"]
  R7 = Resistor [tolerance=±5% resistance=220 package=THT]
  Q4 = NPN-Transistor [package="TO92 [THT]"]
  R8 = Resistor [tolerance=±5% resistance=220 package=THT]
  R9 = Resistor [tolerance=±5% resistance=220 package=THT]
  R10 = Resistor [tolerance=±5% resistance=220 package=THT]
  R11 = Resistor [tolerance=±5% resistance=220 package=THT]
  J1 = male pin header, 5 pins [form="♂ (male)"]
  KEY6 = male pin header, 3 pins [form="♂ (male)"]
  KEY7 = male pin header, 3 pins [form="♂ (male)"]
  KEY8 = male pin header, 3 pins [form="♂ (male)"]
  KEY9 = male pin header, 3 pins [form="♂ (male)"]
  Q5 = NPN-Transistor [package="TO92 [THT]"]
  IC1 = IC, DIP package, 28 pins [chip_label=IC]
  Q6 = NPN-Transistor [package="TO92 [THT]"]
  Q7 = NPN-Transistor [package="TO92 [THT]"]
  Q8 = NPN-Transistor [package="TO92 [THT]"]
  R16 = Resistor [tolerance=±5% resistance=220 package=THT]
  R17 = Resistor [tolerance=±5% resistance=220 package=THT]
  R18 = Resistor [tolerance=±5% resistance=220 package=THT]
  R19 = Resistor [tolerance=±5% resistance=220 package=THT]
  R15 = Resistor [tolerance=±5% resistance=220 package=THT]
  R14 = Resistor [tolerance=±5% resistance=220 package=THT]
  R13 = Resistor [tolerance=±5% resistance=220 package=THT]
  R12 = Resistor [tolerance=±5% resistance=220 package=THT]
  A2 = male pin header, 3 pins [form="♂ (male)"]
  A1 = male pin header, 3 pins [form="♂ (male)"]
  A0 = male pin header, 3 pins [form="♂ (male)"]

nets:
  N1: KEY1.pin1, KEY1.pin2, KEY1.pin3, Q1.E, KEY3.pin3, KEY4.pin2, KEY4.pin3, Q3.E, KEY5.pin3, J1.pin4, IC1.pin1, IC1.pin10
  N2: Q1.B, R11.Pin_0
  N3: Q1.C, R2.Pin_0, R2.Pin_1, R4.Pin_1, R6.Pin_1, R9.Pin_1, J1.pin3, R15.Pin_1, R14.Pin_1, R13.Pin_1, R12.Pin_1
  N4: KEY3.pin1, IC1.pin3
  N5: KEY3.pin2, Q2.E
  N6: Q2.B, R10.Pin_0
  N7: Q2.C, R4.Pin_0
  N8: KEY4.pin1, IC1.pin5
  N9: Q3.B, R7.Pin_0
  N10: Q3.C, R6.Pin_0
  N11: KEY5.pin1, IC1.pin7
  N12: KEY5.pin2, Q4.E
  N13: R7.Pin_1, IC1.pin6
  N14: Q4.B, R8.Pin_0
  N15: Q4.C, R9.Pin_0
  N16: R8.Pin_1, IC1.pin8
  N17: R10.Pin_1, IC1.pin4
  N18: R11.Pin_1, IC1.pin2
  N19: J1.pin1, IC1.pin13
  N20: J1.pin2, IC1.pin12
  N21: J1.pin5, IC1.pin9, IC1.pin18, A2.pin2, A1.pin2, A0.pin2
  N22: KEY6.pin1, KEY7.pin1, KEY8.pin1, KEY8.pin2, KEY9.pin1, Q5.E, A2.pin1, A1.pin1, A0.pin1
  N23: KEY6.pin2, Q7.E
  N24: KEY6.pin3, IC1.pin24
  N25: KEY7.pin2, Q6.E
  N26: KEY7.pin3, IC1.pin26
  N27: KEY8.pin3, IC1.pin28
  N28: KEY9.pin2, Q8.E
  N29: KEY9.pin3, IC1.pin22
  N30: Q5.B, R16.Pin_0
  N31: Q5.C, R12.Pin_0
  N32: IC1.pin15, A0.pin3
  N33: IC1.pin16, A1.pin3
  N34: IC1.pin17, A2.pin3
  N35: IC1.pin21, R19.Pin_1
  N36: IC1.pin23, R18.Pin_1
  N37: IC1.pin25, R17.Pin_1
  N38: IC1.pin27, R16.Pin_1
  N39: Q6.B, R17.Pin_0
  N40: Q6.C, R13.Pin_0
  N41: Q7.B, R18.Pin_0
  N42: Q7.C, R14.Pin_0
  N43: Q8.B, R19.Pin_0
  N44: Q8.C, R15.Pin_0
